// Digital circuit ADDER2bit.dig as structural Verilog
module ADDER2bit (
  input  A1,
  input  A2,
  input  B1,
  input  B2,
  output OUTPUT_C,
  output OUTPUT_B,
  output CARRY_A
);

  wire halfadder_1_p4;

  // HALFADDER halfadder_1: pin names not known; wires that end beside it: A2, B2, OUTPUT_C, halfadder_1_p4
  ADDER1bit adder1bit_1 (.INPUT_CARRY_A(halfadder_1_p4), .B(A1), .C(B1), .OUTPUT_B(OUTPUT_B), .CARRY_A(CARRY_A));
endmodule
