// Digital circuit ADDER3BIT.dig as structural Verilog
module ADDER3BIT (
  input  A1,
  input  A2,
  input  A3,
  input  B1,
  input  B2,
  input  B3,
  output out_7,
  output out_8,
  output out_9,
  output out_10
);

  ADDER2bit adder2bit_1 ();  // open: A1, A2, B1, B2, OUTPUT_C, OUTPUT_B, CARRY_A
  ADDER1bit adder1bit_1 ();  // open: INPUT_CARRY_A, B, C, OUTPUT_B, CARRY_A
endmodule
