// Digital circuit ADDER4bit.dig as structural Verilog
module ADDER4bit (
  input  A1,
  input  A2,
  input  A3,
  input  A4,
  input  B1,
  input  B2,
  input  B3,
  input  B4,
  input  C2,
  output A,
  output B,
  output C,
  output D,
  output E
);

  wire adder2bit_1_a;

  ADDER2bit adder2bit_1 (.A1(A3), .A2(A4), .B1(B3), .B2(B4), .C1(C2), .A(adder2bit_1_a), .B(D), .C(E));
  ADDER2bit adder2bit_2 (.A1(A1), .A2(A2), .B1(B1), .B2(B2), .C1(adder2bit_1_a), .A(A), .B(B), .C(C));
endmodule
