// Digital circuit ANDGate.dig as structural Verilog
module ANDGate (
  input  B,
  input  A,
  output OUTPUT
);

  wire nfet_1_s;

  NFET nfet_1 (.G(A), .D(1'b1), .S(nfet_1_s));
  NFET nfet_2 (.G(B), .D(nfet_1_s), .S(OUTPUT));
endmodule
