// Digital circuit NANDGate.dig as structural Verilog
module NANDGate (
  input  B,
  input  A,
  output OUTPUT
);

  PFET pfet_1 (.G(A), .S(1'b1), .D(OUTPUT));
  PFET pfet_2 (.G(B), .S(1'b1), .D(OUTPUT));
endmodule
