// Digital circuit NORGate.dig as structural Verilog
module NORGate (
  input  B,
  input  A,
  output OUTPUT
);

  wire pfet_1_d;

  PFET pfet_1 (.G(B), .S(1'b1), .D(pfet_1_d));
  PFET pfet_2 (.G(A), .S(pfet_1_d), .D(OUTPUT));
endmodule
