// Digital circuit ORGate.dig as structural Verilog
module ORGate (
  input  A,
  input  B,
  output OUTPUT
);

  NFET nfet_1 (.G(A), .D(1'b1), .S(OUTPUT));
  NFET nfet_2 (.G(B), .D(1'b1), .S(OUTPUT));
endmodule
