// Digital circuit XNORGate.dig as structural Verilog
module XNORGate (
  input  A,
  input  B,
  output out_1
);

  wire pfet_1_d;

  NFET nfet_1 (.G(A), .D(B), .S(out_1));
  PFET pfet_1 (.G(A), .S(1'b1), .D(pfet_1_d));
  PFET pfet_2 (.G(B), .S(pfet_1_d), .D(out_1));
endmodule
