// Digital circuit XORGate.dig as structural Verilog
module XORGate (
  input  A,
  input  B,
  output OUTPUT
);

  wire pfet_1_d;

  PFET pfet_1 (.G(A), .S(1'b1), .D(pfet_1_d));
  NFET nfet_1 (.G(B), .D(OUTPUT), .S(pfet_1_d));
  PFET pfet_2 (.G(B), .S(A), .D(OUTPUT));
endmodule
